# Fritzing sketch ProjetPerso-ESP8266 (saved by Fritzing 0.9.3b)
breadboards: 1

parts:
  LED1 = LED - 3mm [color="Red (633nm)" package="3 mm [THT]"]
  LED2 = LED - 3mm [color="Yellow (592nm)" package="3 mm [THT]"]
  LED3 = LED - 3mm [color="Green (555nm)" package="3 mm [THT]"]
  R1 = Resistor [tolerance=±5% resistance=100 package="0805 [SMD]"]
  R2 = Resistor [tolerance=±5% resistance=100 package="0805 [SMD]"]
  R3 = Resistor [tolerance=±5% resistance=100 package="0805 [SMD]"]
  WeMos_D1_Mini1 = WeMos D1 Mini

nets:
  N1: LED1.cathode, R2.Pin_0
  N2: LED1.anode, WeMos_D1_Mini1.D2
  N3: LED2.cathode, R3.Pin_0
  N4: LED2.anode, WeMos_D1_Mini1.D5
  N5: LED3.cathode, R1.Pin_0
  N6: LED3.anode, WeMos_D1_Mini1.D1
  N7: R1.Pin_1, R2.Pin_1, R3.Pin_1, WeMos_D1_Mini1.G
